# Fritzing sketch CWKeyer (saved by Fritzing 1.0.4)
circuit board: 8.37863cm x 5.73501cm
breadboards: 1

parts:
  ESP8266 = NodeMCU V3.0
  Encoder = male pin header, 5 pins [form="♂ (male)"]
  Battery = male pin header, 2 pins [form="♂ (male)"]
  Keyer = male pin header, 3 pins [form="♂ (male)"]
  Speaker = male pin header, 3 pins [form="♂ (male)"]
  Buzz = Piezo Speaker
  Display = male pin header, 4 pins [form="♂ (male)"]
  Volume = 6mm Trimmer Potentiometer [maximum_resistance=10kΩ knob_status=50% power=0.5W package=THT]
  UART = male pin header, 4 pins [form="♂ (male)"]

nets:
  N1: ESP8266.D0, Encoder.pin3
  N2: ESP8266.D1, Display.pin3
  N3: ESP8266.D2, Display.pin4
  N4: ESP8266.D3, Encoder.pin4
  N5: ESP8266.D4, Encoder.pin5
  N6: ESP8266.3V3, Encoder.pin2, Display.pin2, UART.pin2
  N7: ESP8266.GND, Encoder.pin1, Battery.pin2, Keyer.pin1, Speaker.pin1, Buzz.pin2, Display.pin1, Volume.leg1, UART.pin1
  N8: ESP8266.D5, Volume.leg2
  N9: ESP8266.D6, Keyer.pin2
  N10: ESP8266.D7, Keyer.pin3
  N11: ESP8266.D8, Buzz.pin1
  N12: ESP8266.RX, UART.pin3
  N13: ESP8266.TX, UART.pin4
  N14: ESP8266.Vin, Battery.pin1
  N15: Speaker.pin2, Speaker.pin3, Volume.wiper

notes:
  DL1SKD
  CWKeyer
  Ver 0.5

custom parts:
  NodeMCU V3.0: ESP8266 based NodeMCU
